// Logisim project Computador simulador.circ as structural Verilog
module main (
  input  in_1
);

  wire ADD, CLK, clock_1_out, EQ, GEQ, GT, HLT, JMP, LEQ, LT, MovRxRA, MovRxRy, MUL, not_1_out, RDM, STR, SUB;
  wire [1:0] End_RAM, End_Registrador, Rx, Ry;
  wire [3:0] CONTROLE, OPERACAO;
  wire [4:0] CONTADOR;
  wire [7:0] Input_RAM, RAM, Saida_ROM;

  PC pc_1 (.CONTADOR(CONTADOR), .CLK(CLK), .reset(in_1));
  Clock clock_1 (.out(clock_1_out));
  assign CLK = not_1_out ? clock_1_out : 1'bz;  // Controlled_Buffer controlled_buffer_1
  not not_1 (not_1_out, HLT);
  Register register_1 (.D(Saida_ROM), .Q({CONTROLE, End_Registrador, End_RAM}), .clk(CLK), .clr(in_1));  // open: en
  \Registrador_de_instrução  \registrador_de_instrução_1  (
    .Instrucao_ROM(Saida_ROM), .Ry(Ry), .Rx(Rx), .\Instrução_decodificador (OPERACAO), .CLK(CLK), .clear(in_1));
  \Decode_instruções  \decode_instruções_1  (
    .Operacao(OPERACAO), .EQ(EQ), .LT(LT), .GT(GT), .LEQ(LEQ), .GEQ(GEQ), .JMP(JMP), .MUL(MUL), .ADD(ADD),
    .SUB(SUB), .MovRxRy(MovRxRy), .MovRxRA(MovRxRA), .RDM(RDM), .STR(STR), .HLT(HLT));
  ROM #(.addrWidth(5)) rom_1 (.addr(CONTADOR), .data(Saida_ROM));  // open: sel
  RAM #(.addrWidth(2), .bus("separate")) ram_1 (
    .addr(Ry), .din(Input_RAM), .data(RAM), .str(STR), .clk(CLK), .ld(RDM));  // open: sel, clr

  // Other names for the same wires on the sheet: clear = in_1

  // Notes on the sheet:
  //   CONTADOR DE PROGRAMA
  //   Registrador de Instrução 
  //   END RAM
  //   END REGISTRADOR
  //   Memoria de programa
  //   Memoria Dados
  //   DECODIFICADOR DE INSTRUÇÕES 
  //   INSTRUÇÃO
endmodule

module ULA (
  input  EQ,
  input  [7:0] Entrada_Rx,
  input  LT,
  input  [7:0] Entrada_Ry,
  input  GT,
  input  LEQ,
  input  [7:0] in_7,
  input  GEQ,
  input  ADD,
  input  SUB,
  input  MUL
);

  wire clock, comparator_1_eq, comparator_2_lt, comparator_3_eq, comparator_3_lt, comparator_4_eq,
       comparator_4_gt, comparator_5_gt, controlled_buffer_4_out, or_1_out, or_2_out;
  wire [7:0] adder_1_out, multiplier_1_out, SaidaRx, SaidaRy, subtractor_1_out;

  Register register_1 (.D(Entrada_Rx), .Q(SaidaRx), .clk(clock));  // open: en, clr
  Register register_2 (.D(Entrada_Ry), .Q(SaidaRy), .clk(clock));  // open: en, clr
  Comparator comparator_1 (.a(SaidaRx), .b(SaidaRy), .eq(comparator_1_eq));  // open: gt, lt
  Comparator comparator_2 (.a(SaidaRx), .b(SaidaRy), .lt(comparator_2_lt));  // open: gt, eq
  Comparator comparator_3 (.a(SaidaRx), .b(SaidaRy), .eq(comparator_3_eq), .lt(comparator_3_lt));  // open: gt
  Comparator comparator_4 (.a(SaidaRx), .b(SaidaRy), .gt(comparator_4_gt), .eq(comparator_4_eq));  // open: lt
  Adder adder_1 (.a(SaidaRx), .b(SaidaRy), .out(adder_1_out));  // open: cin, cout
  Subtractor subtractor_1 (.a(SaidaRx), .b(SaidaRy), .out(subtractor_1_out));  // open: bin, bout
  Multiplier multiplier_1 (.a(SaidaRx), .b(SaidaRy), .out(multiplier_1_out));  // open: cin, cout
  Comparator comparator_5 (.a(SaidaRx), .b(SaidaRy), .gt(comparator_5_gt));  // open: eq, lt
  or or_1 (or_1_out, comparator_3_eq, comparator_3_lt);
  or or_2 (or_2_out, comparator_4_gt, comparator_4_eq);
  assign in_7 = ADD ? adder_1_out : 8'bz;  // Controlled_Buffer controlled_buffer_1
  assign in_7 = SUB ? subtractor_1_out : 8'bz;  // Controlled_Buffer controlled_buffer_2
  assign in_7 = MUL ? multiplier_1_out : 8'bz;  // Controlled_Buffer controlled_buffer_3
  assign controlled_buffer_4_out = EQ ? comparator_1_eq : 1'bz;  // Controlled_Buffer controlled_buffer_4
  assign controlled_buffer_4_out = LT ? comparator_2_lt : 1'bz;  // Controlled_Buffer controlled_buffer_5
  assign controlled_buffer_4_out = GT ? comparator_5_gt : 1'bz;  // Controlled_Buffer controlled_buffer_6
  assign controlled_buffer_4_out = LEQ ? or_1_out : 1'bz;  // Controlled_Buffer controlled_buffer_7
  assign controlled_buffer_4_out = GEQ ? or_2_out : 1'bz;  // Controlled_Buffer controlled_buffer_8
  assign in_7 = {{7{1'b0}}, controlled_buffer_4_out};  // Bit_Extender bit_extender_1
endmodule

module PC (
  input  CLK,
  input  reset,
  output [4:0] CONTADOR
);

  Counter #(.width(5), .max('h1f)) counter_1 (.Q(CONTADOR), .clk(CLK), .clr(reset));  // open: load, D, count, carry
endmodule

module \Registrador_de_instrução  (
  input  [7:0] Instrucao_ROM,
  input  CLK,
  input  clear,
  output [1:0] Ry,
  output [1:0] Rx,
  output [3:0] \Instrução_decodificador 
);

  Register #(.trigger("falling")) register_1 (
    .D(Instrucao_ROM), .Q({\Instrução_decodificador , Rx, Ry}), .clk(CLK), .clr(clear));  // open: en

  // Notes on the sheet:
  //   Ex:
  //   ADD RX, RY
  //   Bits mais significativos são da INSTRUÇÃO; do meio Rx, ultimos dois bits Ry
  //   01
  //   1001
  //   end Ram
  //   10
  //   end registrador
endmodule

module Banco_de_registradores (
  input  [1:0] RY,
  input  [7:0] Conteudo_RX,
  input  [1:0] Rx,
  input  [7:0] Conteudo_Ry,
  input  [1:0] Ry_2,
  input  in_6,
  input  reset
);

  wire R0, R1, R2, R3;
  wire [7:0] Out_R0, Out_R1, Out_R2, Out_R3, undriven;

  Decoder #(.select(2)) decoder_1 (.out0(R0), .out1(R1), .out2(R2), .out3(R3), .sel(RY));  // open: en
  Register u_R0 (.D(undriven), .en(R0), .Q(Out_R0), .clk(in_6), .clr(reset));
  Register u_R1 (.D(undriven), .en(R1), .Q(Out_R1), .clk(in_6), .clr(reset));
  Register u_R2 (.D(undriven), .en(R2), .Q(Out_R2), .clk(in_6), .clr(reset));
  Register u_R3 (.D(undriven), .en(R3), .Q(Out_R3), .clk(in_6), .clr(reset));
  Multiplexer #(.select(2), .width(8)) multiplexer_1 (
    .in0(Out_R0), .in1(Out_R1), .in2(Out_R2), .in3(Out_R3), .out(Conteudo_RX), .sel(Rx));  // open: en
  Multiplexer #(.select(2), .width(8)) multiplexer_2 (
    .in0(Out_R0), .in1(Out_R1), .in2(Out_R2), .in3(Out_R3), .out(Conteudo_Ry), .sel(Ry_2));  // open: en

  // Other names for the same wires on the sheet: clear = reset; CLk = in_6

  // Notes on the sheet:
  //   End RAM
endmodule

module \Decode_instruções  (
  input  [3:0] Operacao,
  output EQ,
  output LT,
  output GT,
  output LEQ,
  output GEQ,
  output JMP,
  output MUL,
  output ADD,
  output SUB,
  output MovRxRy,
  output MovRxRA,
  output RDM,
  output STR,
  output HLT
);

  Comparator #(.width(4)) comparator_1 (.a(Operacao), .b(4'b0010), .eq(EQ));  // open: gt, lt
  Comparator #(.width(4)) comparator_2 (.a(Operacao), .b(4'b0011), .eq(LT));  // open: gt, lt
  Comparator #(.width(4)) comparator_3 (.a(Operacao), .b(4'b0100), .eq(GT));  // open: gt, lt
  Comparator #(.width(4)) comparator_4 (.a(Operacao), .b(4'b0101), .eq(LEQ));  // open: gt, lt
  Comparator #(.width(4)) comparator_5 (.a(Operacao), .b(4'b0110), .eq(GEQ));  // open: gt, lt
  Comparator #(.width(4)) comparator_6 (.a(Operacao), .b(4'b0111), .eq(JMP));  // open: gt, lt
  Comparator #(.width(4)) comparator_7 (.a(Operacao), .b(4'b1000), .eq(MUL));  // open: gt, lt
  Comparator #(.width(4)) comparator_8 (.a(Operacao), .b(4'b1001), .eq(ADD));  // open: gt, lt
  Comparator #(.width(4)) comparator_9 (.a(Operacao), .b(4'b1010), .eq(SUB));  // open: gt, lt
  Comparator #(.width(4)) comparator_10 (.a(Operacao), .b(4'b1011), .eq(MovRxRy));  // open: gt, lt
  Comparator #(.width(4)) comparator_11 (.a(Operacao), .b(4'b1100), .eq(MovRxRA));  // open: gt, lt
  Comparator #(.width(4)) comparator_12 (.a(Operacao), .b(4'b1101), .eq(RDM));  // open: gt, lt
  Comparator #(.width(4)) comparator_13 (.a(Operacao), .b(4'b1110), .eq(STR));  // open: gt, lt
  Comparator #(.width(4)) comparator_14 (.a(Operacao), .b(4'b1111), .eq(HLT));  // open: gt, lt
endmodule
